# Fritzing sketch CircuitLayout (saved by Fritzing 0.9.3b)
breadboards: 1

parts:
  Part1 = Arduino Uno (Rev3)
  Part2 = Bluetooth HC-05 Macho
  LED1 = LED - 5mm [color="Red (633nm)" package="5 mm [THT]"]
  R1 = Resistor [tolerance=±5% resistance=220 package="0402 [SMD]"]

nets:
  N1: Part1.D13/SCK, LED1.cathode
  5V: Part1.5V, Part2.VCC
  GND: Part1.GND, Part2.GND
  N2: LED1.anode, R1.Pin_0

// code stored in the sketch: ArduinoWiring.ino
//Code from https://create.arduino.cc/projecthub/user206876468/arduino-bluetooth-basic-tutorial-d8b737
/*
* Bluetooh Basic: LED ON OFF - Avishkar
* Coder - Mayoogh Girish
* Website - http://bit.do/Avishkar
* Download the App : https://github.com/Mayoogh/Arduino-Bluetooth-Basic
* This program lets you to control a LED on pin 13 of arduino using a bluetooth module
*/
char data = 0;            //Variable for storing received data
void setup()
{
    Serial.begin(9600);   //Sets the baud for serial data transmission                               
    pinMode(13, OUTPUT);  //Sets digital pin 13 as output pin
}
void loop()
{
   if(Serial.available() > 0)      // Send data only when you receive data:
   {
      data = Serial.read();        //Read the incoming data & store into data
      Serial.print(data);          //Print Value inside data in Serial monitor
      Serial.print("\n");        
      if(data == '1')              // Checks whether value of data is equal to 1
         digitalWrite(13, HIGH);   //If value is 1 then LED turns ON
      else if(data == '0')         //  Checks whether value of data is equal to 0
         digitalWrite(13, LOW);    //If value is 0 then LED turns OFF
   }
}
